// Logisim project PROJECT.circ as structural Verilog: 1 circuit, main circuit main
module main (
  input  [3:0] S3S2S1S0,
  input  [7:0] A,
  input  [7:0] B,
  output C,
  output V,
  output N,
  output [7:0] F,
  output Z
);

  wire and_2_out, and_3_out;
  wire [0:0] not_3_out;
  wire [6:0] adder_1_out;
  wire [7:0] and_1_out, multiplexer_1_out, multiplexer_2_out, not_1_out, not_2_out, xor_1_out;

  assign not_1_out = ~B;  // NOT_Gate not_1, 8 bits wide
  assign not_2_out = ~A;  // NOT_Gate not_2, 8 bits wide
  Multiplexer #(.select(2), .width(8), .enable("false")) multiplexer_1 (
    .in0({8{1'b1}}), .in1(not_1_out), .in2(B), .in3(8'h3), .out(multiplexer_1_out), .sel(S3S2S1S0[2:1]));
  assign xor_1_out = A ^ B;  // XOR_Gate xor_1, 8 bits wide
  assign and_1_out = A & B;  // AND_Gate and_1, 8 bits wide
  not not_3 (not_3_out[0], A[7]);
  Multiplexer #(.select(3), .width(8)) multiplexer_2 (
    .in0(xor_1_out), .in1(not_1_out), .in2(and_1_out), .in3(not_2_out), .in4(B), .in5({B[6:0], 1'b0}),
    .in6({{2{B[7]}}, B[6:1]}), .in7({A[6:0], not_3_out[0]}), .out(multiplexer_2_out), .en(S3S2S1S0[0]));  // open: sel
  Adder adder_1 (.a(A), .b(multiplexer_1_out), .out({N, adder_1_out}), .cin(S3S2S1S0[0]), .cout(C));
  Multiplexer #(.width(8), .enable("false")) multiplexer_3 (
    .in0({N, adder_1_out}), .in1(multiplexer_2_out), .out(F), .sel(S3S2S1S0[3]));
  and and_2 (and_2_out, N, ~A[7], ~multiplexer_1_out[7]);  // AND_Gate
  and and_3 (and_3_out, ~N, A[7], multiplexer_1_out[7]);  // AND_Gate
  or or_1 (V, and_2_out, and_3_out);
  nor nor_1 (Z, F[0], F[1], F[2], F[3], F[4], F[5], F[6], F[7]);
endmodule
